// Logisim project ECE_649_Final_Project_Sam_Green_Josh_Grimes.circ as structural Verilog: 1 circuit, main circuit main
module main (
  input  rst
);

  wire and_1_out, and_2_out, and_3_out, and_4_out, clk_out, comparator_1_eq, decoder_1_out0, decoder_1_out1,
       decoder_1_out2, decoder_1_out3, decoder_2_out4, decoder_2_out8, decoder_2_out12, decoder_2_out20,
       decoder_2_out24, not_1_out, or_1_out;
  wire [1:0] bit_extender_2_out, bit_extender_4_out, InMEM_dout, InMEM_dout_4;
  wire [2:0] InMEM_dout_5;
  wire [4:0] InMEM_dout_2;
  wire [7:0] adder_1_out, adder_2_out, bit_extender_1_out, bit_extender_6_out, multiplexer_1_out, PC_q;
  wire [11:0] InMEM_dout_6;
  wire [19:12] InMEM_dout_3;
  wire [31:0] adder_3_out, adder_4_out, bit_extender_3_out, bit_extender_5_out, multiplexer_2_out,
       multiplexer_3_out, multiplexer_4_out, undriven, x0_q, x1_q, x2_q, x3_q;

  Clock clk (.out(clk_out));
  Register PC (.D(multiplexer_1_out), .clk(clk_out), .Q(PC_q), .clr(rst));  // open: en
  Bit_Extender #(.in_width(13), .out_width(8), .\type ("zero")) bit_extender_1 (
    .in({InMEM_dout_6[11], InMEM_dout_6[0], InMEM_dout_6[10:1], 1'b0}), .out(bit_extender_1_out));
  Adder adder_1 (.a(bit_extender_1_out), .b(PC_q), .out(adder_1_out));  // open: cin, cout
  Adder adder_2 (.a(8'h1), .b(PC_q), .out(adder_2_out));  // open: cin, cout
  RAM #(.dataWidth(32)) InMEM (
    .addr(PC_q), .we(1'b0), .oe(1'b1), .clk(clk_out), .din(undriven),
    .dout({InMEM_dout_6[11:5], InMEM_dout_5, InMEM_dout_4, InMEM_dout_3, InMEM_dout_6[4:0], InMEM_dout_2, InMEM_dout}));
  RAM #(.dataWidth(32)) DataMem (
    .addr(bit_extender_6_out), .we(decoder_2_out8), .oe(1'b1), .clk(clk_out), .din(multiplexer_3_out));  // open: dout
  Multiplexer #(.width(8)) multiplexer_1 (
    .in0(adder_2_out), .in1(adder_1_out), .out(multiplexer_1_out), .sel(and_4_out));
  Bit_Extender #(.in_width(5), .out_width(2), .\type ("zero")) bit_extender_2 (
    .in(InMEM_dout_6[4:0]), .out(bit_extender_2_out));
  assign bit_extender_3_out = {{20{1'b0}}, InMEM_dout_6};  // Bit_Extender bit_extender_3
  Decoder #(.select(2)) decoder_1 (
    .out0(decoder_1_out0), .out1(decoder_1_out1), .out2(decoder_1_out2), .out3(decoder_1_out3),
    .sel(bit_extender_2_out), .en(1'b1));
  Bit_Extender #(.in_width(5), .out_width(2), .\type ("zero")) bit_extender_4 (
    .in(InMEM_dout_3[19:15]), .out(bit_extender_4_out));
  Register #(.width(32)) x0 (.D(adder_3_out), .en(1'b0), .clk(clk_out), .Q(x0_q), .clr(rst));
  Register #(.width(32)) x1 (.D(adder_3_out), .en(and_1_out), .clk(clk_out), .Q(x1_q), .clr(rst));
  and and_1 (and_1_out, decoder_1_out1, or_1_out);
  Register #(.width(32)) x2 (.D(adder_3_out), .en(and_2_out), .clk(clk_out), .Q(x2_q), .clr(rst));
  and and_2 (and_2_out, decoder_1_out2, or_1_out);
  Register #(.width(32)) x3 (.D(adder_3_out), .en(and_3_out), .clk(clk_out), .Q(x3_q), .clr(rst));
  and and_3 (and_3_out, decoder_1_out3, or_1_out);
  Multiplexer #(.select(2), .width(32)) multiplexer_2 (
    .in0(x0_q), .in1(x1_q), .in2(x2_q), .in3(x3_q), .out(multiplexer_2_out), .sel(bit_extender_4_out));
  Multiplexer #(.select(2), .width(32)) multiplexer_3 (
    .in0(x0_q), .in1(x1_q), .in2(x2_q), .in3(x3_q), .out(multiplexer_3_out), .sel(InMEM_dout_4));
  assign bit_extender_5_out = {{20{1'b0}}, {InMEM_dout_6[11:5], InMEM_dout_5, InMEM_dout_4}};  // Bit_Extender bit_extender_5
  Multiplexer #(.width(32)) multiplexer_4 (
    .in0(multiplexer_3_out), .in1(bit_extender_5_out), .out(multiplexer_4_out), .sel(not_1_out));
  and and_4 (and_4_out, decoder_2_out24, comparator_1_eq);
  Comparator #(.mode("unsigned"), .width(32)) comparator_1 (
    .a(multiplexer_2_out), .b(multiplexer_3_out), .eq(comparator_1_eq));  // open: gt, lt
  Adder #(.width(32)) adder_3 (
    .a(multiplexer_2_out), .b(multiplexer_4_out), .out(adder_3_out), .cin(1'b0));  // open: cout
  Adder #(.width(32)) adder_4 (.a(multiplexer_2_out), .b(bit_extender_3_out), .out(adder_4_out));  // open: cin, cout
  Bit_Extender #(.in_width(32), .out_width(8), .\type ("zero")) bit_extender_6 (
    .in(adder_4_out), .out(bit_extender_6_out));
  or or_1 (or_1_out, decoder_2_out4, decoder_2_out12);
  LED led_1 (.in(decoder_2_out8));
  not not_1 (not_1_out, decoder_2_out4);
  LED led_2 (.in(decoder_2_out4));
  LED led_3 (.in(decoder_2_out12));
  LED led_4 (.in(decoder_2_out24));
  Decoder #(.select(5)) decoder_2 (
    .out4(decoder_2_out4), .out8(decoder_2_out8), .out12(decoder_2_out12), .out20(decoder_2_out20),
    .out24(decoder_2_out24), .sel(InMEM_dout_2), .en(1'b1));  // open: out0, out1, out2, out3, out5, out6, out7, out9, out10, out11, out13, out14, out15, out16, out17, out18, out19, out21, out22, out23, out25, out26, out27, out28, out29, out30, out31

  // Notes on the sheet:
  //   pc_offset
  //   1: branch; 0: no-branch
  //   fun7
  //   offset 10:5
  //   offset 12
  //   rd
  //   fun3
  //   offset[4-0]
  //   offset[11-5]
  //   offset 11
  //   opcode
  //   rs1
  //   rs2
  //   Imm
  //   offset 4:1
  //   write_reg
  //   data_rs2
  //   write_data
  //   clk_sig
  //   rst_sig
  //   read_reg1
  //   read_reg2
  //   read_data1
  //   read_data2
  //   sw_addr
  //   addi
  //   sw
  //   add
  //   beq
  //   Control
endmodule
